// Logisim project File IT012_Lab01_24521217.circ as structural Verilog: 5 circuits, main circuit main
module main (
  input  in_1,
  input  in_2,
  output out_3
);

  wire not_1_out;

  not not_1 (not_1_out, in_2);
  and and_1 (out_3, in_1, not_1_out);
endmodule

module Warmup (
  input  A,
  input  F,
  input  B
);

  wire not_1_out;

  not not_1 (not_1_out, B);
  and and_1 (F, A, not_1_out);
endmodule

module TN1 (
  input  A,
  input  B,
  input  C,
  output NOT,
  output AND,
  output OR,
  output NAND,
  output NOR,
  output XOR,
  output XNOR,
  output XOR3,
  output NAND3,
  output CHAIN
);

  wire nand_3_out;

  not not_1 (NOT, A);
  and and_1 (AND, A, B);
  or or_1 (OR, A, B);
  nand nand_1 (NAND, A, B);
  nor nor_1 (NOR, A, B);
  xor xor_1 (XOR, A, B);
  xnor xnor_1 (XNOR, A, B);
  ExactlyOne xor_2 (.out(XOR3), .in0(A), .in1(B), .in2(C));
  nand nand_2 (NAND3, A, B, C);
  nand nand_3 (nand_3_out, A, B);
  nand nand_4 (CHAIN, nand_3_out, C);
endmodule

module TN2 (
  input  x,
  input  y,
  input  z,
  output EQ1,
  output EQ2,
  output EQ3,
  output EQ4,
  output EQ5
);

  wire x_prime_2_out, x_prime_out, x_prime_y_out, x_prime_y_prime_out, x_x_prime_y_out, x_y_2_out,
       x_y__prime_out, x_y__x_z_out, x_y_out, x_yz_out, x_z_out, xy__prime_out, y_prime_out, yz_out;

  not x_prime (x_prime_out, x);
  not y_prime (y_prime_out, y);
  not x_prime_2 (x_prime_2_out, x);
  or x_y (x_y_out, x, y);
  not x_y__prime (x_y__prime_out, x_y_out);
  and x_y_2 (x_y_2_out, x, y);
  and yz (yz_out, y, z);
  or x_z (x_z_out, x, z);
  and x_prime_y (x_prime_y_out, x_prime_2_out, y);
  and x_prime_y_prime (x_prime_y_prime_out, x_prime_out, y_prime_out);
  not xy__prime (xy__prime_out, x_y_2_out);
  or x_yz (x_yz_out, yz_out, x);
  and x_y__x_z (x_y__x_z_out, x_y_out, x_z_out);
  or x_x_prime_y (x_x_prime_y_out, x_prime_y_out, x);
  xnor xnor_1 (EQ1, x_y__prime_out, x_prime_y_prime_out);
  xnor xnor_2 (EQ2, x_prime_y_prime_out, xy__prime_out);
  xnor xnor_3 (EQ3, x_yz_out, x_y__x_z_out);
  xnor xnor_4 (EQ4, x_x_prime_y_out, x);
  xnor xnor_5 (EQ5, x_x_prime_y_out, x_y_out);
endmodule

module TN3 (
  input  A,
  input  B,
  input  C,
  input  D,
  output F
);

  wire m2_A_prime_B_prime_CD_prime_out, m3_A_prime_B_prime_CD_out, m5_A_prime_BC_prime_D_out,
       m7_A_prime_BCD_out, m11_AB_prime_CD_out, m13_ABC_prime_D_out, not_1_out, not_2_out, not_3_out,
       not_4_out;

  not not_1 (not_1_out, A);
  not not_2 (not_2_out, B);
  not not_3 (not_3_out, C);
  not not_4 (not_4_out, D);
  and m2_A_prime_B_prime_CD_prime (m2_A_prime_B_prime_CD_prime_out, not_1_out, not_2_out, C, not_4_out);
  and m3_A_prime_B_prime_CD (m3_A_prime_B_prime_CD_out, not_1_out, not_2_out, C, D);
  and m5_A_prime_BC_prime_D (m5_A_prime_BC_prime_D_out, not_1_out, B, not_3_out, D);
  and m7_A_prime_BCD (m7_A_prime_BCD_out, not_1_out, B, C, D);
  and m11_AB_prime_CD (m11_AB_prime_CD_out, A, not_2_out, C, D);
  and m13_ABC_prime_D (m13_ABC_prime_D_out, A, B, not_3_out, D);
  or or_1 (F, m2_A_prime_B_prime_CD_prime_out, m3_A_prime_B_prime_CD_out, m5_A_prime_BC_prime_D_out, m7_A_prime_BCD_out, m11_AB_prime_CD_out, m13_ABC_prime_D_out);
endmodule
