// Logisim project IT012_Lab02_24521217.circ as structural Verilog
module warmup (
  input  [7:0] A,
  input  [7:0] B,
  output [7:0] S
);

  wire adder_1_cout;

  Adder adder_1 (.a(A), .b(B), .out(S), .cin(1'b0), .cout(adder_1_cout));
  // Probe on adder_1_cout
  // Probe on S
endmodule

module FA (
  input  A,
  input  B,
  input  Cin,
  output S,
  output Cout
);

  wire AND_2_out, AND_out, XOR1_out;

  xor XOR1 (XOR1_out, A, B);
  and AND (AND_out, A, B);
  and AND_2 (AND_2_out, XOR1_out, Cin);
  xor XOR2 (S, Cin, XOR1_out);
  or OR (Cout, AND_out, AND_2_out);
endmodule

module ADDSUB4 (
  input  [3:0] A,
  input  [3:0] B,
  input  SUB,
  output Z,
  output [3:0] S,
  output N,
  output C,
  output V
);

  wire FA0_cout, FA1_cout, FA2_cout, XOR0_out, XOR1_out, XOR2_out, XOR3_out, XOR_2_out, XOR_out;

  xor XOR0 (XOR0_out, B[0], SUB);
  xor XOR1 (XOR1_out, B[1], SUB);
  xor XOR2 (XOR2_out, B[2], SUB);
  xor XOR3 (XOR3_out, B[3], SUB);
  FA FA0 (.A(A[0]), .B(XOR0_out), .Cin(SUB), .S(S[0]), .Cout(FA0_cout));
  // Probe on FA0_cout
  FA FA1 (.A(A[1]), .B(XOR1_out), .Cin(FA0_cout), .S(S[1]), .Cout(FA1_cout));
  // Probe on FA1_cout
  FA FA2 (.A(A[2]), .B(XOR2_out), .Cin(FA1_cout), .S(S[2]), .Cout(FA2_cout));
  // Probe on FA2_cout
  FA FA3 (.A(A[3]), .B(XOR3_out), .Cin(FA2_cout), .S(N), .Cout(C));
  xor XOR (XOR_out, A[3], N);
  xor XOR_2 (XOR_2_out, XOR3_out, N);
  and AND (V, XOR_out, XOR_2_out);
  nor NOR (Z, S[0], S[1], S[2], N);

  assign S[3] = N;
endmodule

module ALU8 (
  input  [7:0] A,
  input  [7:0] B,
  input  [2:0] OP,
  output LT,
  output Z,
  output [7:0] R
);

  wire [7:0] adder_1_out, adder_2_out, AND_out, multiplexer_1_out, multiplexer_2_out, NOT_out, OR_out,
       subtractor_1_out, subtractor_2_out, XOR_out;

  Adder adder_1 (.a(A), .b(B), .out(adder_1_out), .cin(1'b0));  // open: cout
  Adder adder_2 (.a(A), .b(8'h1), .out(adder_2_out), .cin(1'b0));  // open: cout
  Subtractor subtractor_1 (.a(A), .b(B), .out(subtractor_1_out), .bin(1'b0));  // open: bout
  Subtractor subtractor_2 (.a(A), .b(8'h1), .out(subtractor_2_out), .bin(1'b0));  // open: bout
  assign AND_out = A & B;  // AND_Gate AND, 8 bits wide
  assign OR_out = A | B;  // OR_Gate OR, 8 bits wide
  assign NOT_out = ~A;  // NOT_Gate NOT, 8 bits wide
  assign XOR_out = A ^ B;  // XOR_Gate XOR, 8 bits wide
  Multiplexer #(.select(2), .width(8), .enable("false")) multiplexer_1 (
    .in0(adder_1_out), .in1(adder_2_out), .in2(subtractor_1_out), .in3(subtractor_2_out),
    .out(multiplexer_1_out), .sel(OP[1:0]));
  Multiplexer #(.select(2), .width(8), .enable("false")) multiplexer_2 (
    .in0(AND_out), .in1(OR_out), .in2(NOT_out), .in3(XOR_out), .out(multiplexer_2_out), .sel(OP[1:0]));
  // Probe on multiplexer_1_out
  Multiplexer #(.width(8), .enable("false")) multiplexer_3 (
    .in0(multiplexer_1_out), .in1(multiplexer_2_out), .out(R), .sel(OP[2]));
  LT u_LT (.A7(A[7]), .B7(B[7]), .R7(R[7]), .LT(LT));
  nor NOR (Z, R[0], R[1], R[2], R[3], R[4], R[5], R[6], R[7]);
endmodule

module LT (
  input  A7,
  input  B7,
  input  R7,
  output LT
);

  wire AND1_out, AND2_out, AND3_out, not_1_out;

  not not_1 (not_1_out, B7);
  and AND1 (AND1_out, A7, not_1_out);
  and AND2 (AND2_out, A7, R7);
  and AND3 (AND3_out, not_1_out, R7);
  or OR (LT, AND1_out, AND2_out, AND3_out);
endmodule

module DLATCH (
  input  D,
  input  E,
  output Q
);

  Multiplexer #(.enable("false")) multiplexer_1 (.in0(Q), .in1(D), .out(Q), .sel(E));
endmodule

module TN3 (
  input  D,
  input  CLK,
  output Q1,
  output Q2,
  output Q3,
  output QL1,
  output QL2,
  output QF1,
  output QF2
);

  DLATCH DLATCH (.D(D), .E(CLK), .Q(Q1));
  D_Flip_Flop DFF (.clk(CLK), .D(D), .Q(Q2));  // open: Qn, preset, en, reset
  DFF_MS DFF_MS (.D(D), .CLK(CLK), .Q(Q3));
  DLATCH DLATCH1 (.D(D), .E(CLK), .Q(QL1));
  D_Flip_Flop DFF1 (.clk(CLK), .D(D), .Q(QF1));  // open: Qn, preset, en, reset
  DLATCH DLATCH2 (.D(QL1), .E(CLK), .Q(QL2));
  D_Flip_Flop DFF2 (.clk(CLK), .D(QF1), .Q(QF2));  // open: Qn, preset, en, reset
endmodule

module DFF_MS (
  input  D,
  input  CLK,
  output Q
);

  wire MASTER_q, not_1_out;

  DLATCH MASTER (.D(D), .E(not_1_out), .Q(MASTER_q));
  not not_1 (not_1_out, CLK);
  DLATCH SLAVE (.D(MASTER_q), .E(CLK), .Q(Q));
endmodule

module REGFILE (
  input  [7:0] DIN,
  input  CLK,
  input  [1:0] RA,
  input  WE,
  input  [1:0] RD,
  input  [1:0] RB,
  output [7:0] QA,
  output [7:0] R0,
  output [7:0] R1,
  output [7:0] R2,
  output [7:0] R3,
  output [7:0] QB
);

  wire decoder_1_out0, decoder_1_out1, decoder_1_out2, decoder_1_out3;

  Decoder #(.select(2), .disabled(0)) decoder_1 (
    .out0(decoder_1_out0), .out1(decoder_1_out1), .out2(decoder_1_out2), .out3(decoder_1_out3), .sel(RD),
    .en(WE));
  Register u_R0 (.D(DIN), .en(decoder_1_out0), .Q(R0), .clk(CLK), .clr(1'b0));
  Register u_R1 (.D(DIN), .en(decoder_1_out1), .Q(R1), .clk(CLK), .clr(1'b0));
  Register u_R2 (.D(DIN), .en(decoder_1_out2), .Q(R2), .clk(CLK), .clr(1'b0));
  Register u_R3 (.D(DIN), .en(decoder_1_out3), .Q(R3), .clk(CLK), .clr(1'b0));
  Multiplexer #(.select(2), .width(8)) multiplexer_1 (
    .in0(R0), .in1(R1), .in2(R2), .in3(R3), .out(QA), .sel(RA));  // open: en
  Multiplexer #(.select(2), .width(8)) multiplexer_2 (
    .in0(R0), .in1(R1), .in2(R2), .in3(R3), .out(QB), .sel(RB));  // open: en
endmodule

module DATAPATH (
  input  CLK,
  input  WE,
  input  [1:0] RD,
  input  [1:0] RA,
  input  [1:0] RB,
  input  [2:0] OP,
  input  [7:0] IMM,
  input  SRC,
  output [7:0] R0,
  output [7:0] R1,
  output [7:0] R2,
  output [7:0] R3,
  output [7:0] R,
  output Z
);

  wire [7:0] multiplexer_1_out, REGFILE_qa, REGFILE_qb;

  REGFILE REGFILE (
    .DIN(multiplexer_1_out), .CLK(CLK), .WE(WE), .RD(RD), .RA(RA), .RB(RB), .QA(REGFILE_qa), .R0(R0),
    .R1(R1), .R2(R2), .R3(R3), .QB(REGFILE_qb));
  ALU8 ALU8 (.A(REGFILE_qa), .B(REGFILE_qb), .OP(OP), .Z(Z), .R(R));  // open: LT
  Multiplexer #(.width(8), .enable("false")) multiplexer_1 (.in0(R), .in1(IMM), .out(multiplexer_1_out), .sel(SRC));
endmodule
